// Digital circuit OR.dig as structural Verilog
module OR (
  input  in_1,
  input  in_2,
  input  in_3,
  input  B,
  input  in_5,
  input  in_6,
  input  in_7,
  input  in_8
);

  wire and_1_out, fgpfet_1_d, nfet_1_s, nfet_2_s, or_1_out;

  FGPFET fgpfet_1 (.G(in_2), .S(in_1), .D(fgpfet_1_d));
  NFET nfet_1 (.G(in_3), .D(1'b1), .S(nfet_1_s));
  NFET nfet_2 (.G(nfet_1_s), .D(B), .S(nfet_2_s));
  LED C (.in(nfet_2_s));
  LED led_1 (.in(fgpfet_1_d));
  and and_1 (and_1_out, in_5, in_6);
  or or_1 (or_1_out, in_7, in_8);
  LED led_2 (.in(and_1_out));
  LED led_3 (.in(or_1_out));
endmodule
