// Digital circuit christmasTree_circuit.dig as structural Verilog
module christmasTree_circuit (
  input  clk,
  input  in_2,
  output [2:0] out_3,
  output [2:0] out_4
);

  wire counter_1_ovf, decoder_1_out_0, decoder_1_out_1, decoder_1_out_2, decoder_1_out_3, delay_1_out,
       register_1_q, register_2_q, register_3_q, register_4_q;

  Counter #(.Bits(3)) counter_1 (.en(1'b1), .C(clk), .clr(in_2), .out(out_4), .ovf(counter_1_ovf));
  LED led_1 (.in(counter_1_ovf));
  Delay delay_1 (.in(clk), .out(delay_1_out));
  ROM #(.AddrBits(3), .Bits(3)) rom_1 (.A(out_4), .sel(1'b1), .D(out_3));
  Decoder #(.Selector_Bits(2)) decoder_1 (
    .sel(out_3[2:1]), .out_0(decoder_1_out_0), .out_1(decoder_1_out_1), .out_2(decoder_1_out_2),
    .out_3(decoder_1_out_3));
  Register register_1 (.D(out_3[0]), .C(delay_1_out), .en(decoder_1_out_0), .Q(register_1_q));
  Register register_2 (.D(out_3[0]), .C(delay_1_out), .en(decoder_1_out_1), .Q(register_2_q));
  Register register_3 (.D(out_3[0]), .C(delay_1_out), .en(decoder_1_out_2), .Q(register_3_q));
  Register register_4 (.D(out_3[0]), .C(delay_1_out), .en(decoder_1_out_3), .Q(register_4_q));
  LED led_2 (.in(register_1_q));
  LED led_3 (.in(register_2_q));
  LED led_4 (.in(register_3_q));
  LED led_5 (.in(register_4_q));

  // Notes on the sheet:
  //   contents of rom_1 (hex, n*v repeats v):
  //   4,1,3,5,4,7,5
endmodule
