// Digital circuit exercise_2.dig as structural Verilog
module exercise_2 (
  input  B,
  input  A,
  input  A_2,
  input  B_2,
  input  in_5,
  input  in_6,
  input  in_7,
  input  in_8,
  input  in_9,
  input  in_10,
  input  in_11,
  input  [2:0] in_12,
  input  RESET,
  input  SET,
  input  IN,
  input  in_18,
  input  [2:0] in_19,
  input  IN_2,
  input  in_22,
  input  in_23,
  input  IN_3,
  input  QUARTZ,
  input  clk,
  input  in_30,
  output [2:0] out_13,
  output [2:0] out_16,
  output [2:0] out_20,
  output [2:0] out_24,
  output [2:0] out_25,
  output [2:0] out_27,
  output [2:0] out_31,
  output [2:0] out_32
);

  wire and_1_out, and_2_out, and_3_out, and_4_out, and_5_out, counter_1_ovf, counter_2_ovf, counter_3_ovf,
       decoder_1_out_0, decoder_1_out_1, decoder_1_out_2, decoder_1_out_3, decoder_2_out_0, decoder_2_out_1,
       decoder_2_out_2, decoder_2_out_3, delay_1_out, nfet_1_s, nfet_2_s, nor_1_out, nor_2_out, not_1_out,
       not_2_out, not_3_out, not_4_out, not_5_out, pfet_1_d, register_2_q, register_3_q, register_4_q,
       register_5_q, register_6_q, register_7_q, register_8_q, register_9_q;
  wire [2:0] register_1_q;

  PFET pfet_1 (.G(A), .S(B), .D(pfet_1_d));
  Counter #(.Bits(3)) counter_1 (.en(1'b1), .C(clk), .clr(in_30), .out(out_32), .ovf(counter_1_ovf));
  NFET nfet_1 (.G(A_2), .D(1'b1), .S(nfet_1_s));
  NFET nfet_2 (.G(nfet_1_s), .D(B_2), .S(nfet_2_s));
  not not_1 (not_1_out, in_8);
  not not_2 (not_2_out, in_9);
  not not_3 (not_3_out, in_10);
  not not_4 (not_4_out, in_11);
  Counter #(.Bits(3)) counter_2 (.en(in_23), .C(in_22), .clr(IN_2), .out(out_24), .ovf(counter_2_ovf));
  Counter #(.Bits(3)) counter_3 (.en(1'b1), .C(QUARTZ), .clr(IN_3), .out(out_27), .ovf(counter_3_ovf));
  LED C (.in(nfet_2_s));
  LED led_1 (.in(in_8));
  LED led_2 (.in(not_1_out));
  LED led_3 (.in(in_9));
  LED led_4 (.in(not_2_out));
  ROM #(.AddrBits(3), .Bits(3)) Cartuccia (.A(in_12), .sel(1'b1), .D(out_13));
  Register #(.Bits(3)) register_1 (.D(in_19), .C(in_18), .en(IN), .Q(register_1_q));
  LED led_5 (.in(counter_3_ovf));
  LED led_6 (.in(counter_1_ovf));
  LED led_7 (.in(pfet_1_d));
  nor nor_1 (nor_1_out, RESET, nor_2_out);
  nor nor_2 (nor_2_out, nor_1_out, SET);
  LED led_8 (.in(counter_2_ovf));
  Delay delay_1 (.in(clk), .out(delay_1_out));
  ROM #(.AddrBits(3), .Bits(3)) Cartuccia_2 (.A(out_24), .sel(1'b1), .D(out_20));
  ROM #(.AddrBits(3), .Bits(3)) Cartuccia_3 (.A(out_27), .sel(1'b1), .D(out_25));
  ROM #(.AddrBits(3), .Bits(3)) rom_1 (.A(out_32), .sel(1'b1), .D(out_31));
  ROM #(.AddrBits(3), .Bits(3)) Cartuccia_4 (.A(register_1_q), .sel(1'b1), .D(out_16));
  LED led_9 (.in(nor_1_out));
  LED led_10 (.in(nor_2_out));
  not not_5 (not_5_out, in_5);
  and and_1 (and_1_out, in_6, in_7);
  and and_2 (and_2_out, not_3_out, not_4_out);
  and and_3 (and_3_out, in_10, not_4_out);
  and and_4 (and_4_out, in_11, not_4_out);
  and and_5 (and_5_out, in_10, in_11);
  LED led_11 (.in(out_25[0]));
  LED led_12 (.in(not_5_out));
  LED led_13 (.in(and_1_out));
  Decoder #(.Selector_Bits(2)) decoder_1 (
    .sel(out_25[2:1]), .out_0(decoder_1_out_0), .out_1(decoder_1_out_1), .out_2(decoder_1_out_2),
    .out_3(decoder_1_out_3));
  Decoder #(.Selector_Bits(2)) decoder_2 (
    .sel(out_31[2:1]), .out_0(decoder_2_out_0), .out_1(decoder_2_out_1), .out_2(decoder_2_out_2),
    .out_3(decoder_2_out_3));
  LED led_14 (.in(and_2_out));
  LED led_15 (.in(and_3_out));
  Register register_2 (.D(out_25[0]), .C(QUARTZ), .en(decoder_1_out_0), .Q(register_2_q));
  Register register_3 (.D(out_25[0]), .C(QUARTZ), .en(decoder_1_out_1), .Q(register_3_q));
  Register register_4 (.D(out_25[0]), .C(QUARTZ), .en(decoder_1_out_2), .Q(register_4_q));
  Register register_5 (.D(out_25[0]), .C(QUARTZ), .en(decoder_1_out_3), .Q(register_5_q));
  Register register_6 (.D(out_31[0]), .C(delay_1_out), .en(decoder_2_out_0), .Q(register_6_q));
  Register register_7 (.D(out_31[0]), .C(delay_1_out), .en(decoder_2_out_1), .Q(register_7_q));
  Register register_8 (.D(out_31[0]), .C(delay_1_out), .en(decoder_2_out_2), .Q(register_8_q));
  Register register_9 (.D(out_31[0]), .C(delay_1_out), .en(decoder_2_out_3), .Q(register_9_q));
  LED led_16 (.in(and_4_out));
  LED led_17 (.in(and_5_out));
  LED led_18 (.in(register_2_q));
  LED led_19 (.in(register_3_q));
  LED led_20 (.in(register_4_q));
  LED led_21 (.in(register_5_q));
  LED led_22 (.in(register_6_q));
  LED led_23 (.in(register_7_q));
  LED led_24 (.in(register_8_q));
  LED led_25 (.in(register_9_q));

  // Notes on the sheet:
  //   contents of Cartuccia (hex, n*v repeats v):
  //   0,1,1,1,0,1,1
  //   contents of Cartuccia_2 (hex, n*v repeats v):
  //   0,1,1,1,0,1,1
  //   contents of Cartuccia_3 (hex, n*v repeats v):
  //   0,1,1,1,0,1,1
  //   contents of rom_1 (hex, n*v repeats v):
  //   4,1,3,5,4,7,5
  //   contents of Cartuccia_4 (hex, n*v repeats v):
  //   0,1,1,1,0,1,1
endmodule
