// Digital circuit fullAdder.dig as structural Verilog
module fullAdder (
  input  CI,
  input  A,
  input  B,
  output S,
  output CO
);

  wire halfadder_1_c, halfadder_1_s, halfadder_2_c;

  HalfAdder halfadder_1 (.A(A), .B(B), .S(halfadder_1_s), .C(halfadder_1_c));
  HalfAdder halfadder_2 (.A(CI), .B(halfadder_1_s), .S(S), .C(halfadder_2_c));
  or or_1 (CO, halfadder_2_c, halfadder_1_c);

  // Notes on the sheet:
  //   CO: Carry in output
endmodule
