// Digital circuit fullAdder4bit.dig as structural Verilog
module fullAdder4bit (
  input  A1,
  input  B1,
  input  A2,
  input  B2,
  input  A3,
  input  B3,
  input  A0,
  input  B0,
  input  CI,
  output S3,
  output SO,
  output S1,
  output S2,
  output CO
);

  wire fulladder_1_co, fulladder_2_co, fulladder_3_co;

  fullAdder fulladder_1 (.CI(CI), .A(A0), .B(B0), .S(SO), .CO(fulladder_1_co));
  fullAdder fulladder_2 (.CI(fulladder_1_co), .A(A1), .B(B1), .S(S1), .CO(fulladder_2_co));
  fullAdder fulladder_3 (.CI(fulladder_2_co), .A(A2), .B(B2), .S(S2), .CO(fulladder_3_co));
  fullAdder fulladder_4 (.CI(fulladder_3_co), .A(A3), .B(B3), .S(S3), .CO(CO));

  // Notes on the sheet:
  //   FULL ADDER 4 bits
endmodule
