// Digital circuit fullAdder8bit.dig as structural Verilog
module fullAdder8bit (
  input  B7,
  input  A7,
  input  B6,
  input  A6,
  input  B5,
  input  A5,
  input  B4,
  input  A4,
  input  B3,
  input  A3,
  input  B2,
  input  A2,
  input  B1,
  input  A1,
  input  B0,
  input  A0,
  output S7,
  output S6,
  output S5,
  output S4,
  output S3,
  output S2,
  output S1,
  output S0,
  output CO
);

  wire fulladder_1_co, fulladder_2_co, fulladder_3_co, fulladder_4_co, fulladder_5_co, fulladder_6_co,
       fulladder_7_co;

  fullAdder fulladder_1 (.CI(1'b0), .A(A7), .B(B7), .S(S7), .CO(fulladder_1_co));
  fullAdder fulladder_2 (.CI(fulladder_1_co), .A(A6), .B(B6), .S(S6), .CO(fulladder_2_co));
  fullAdder fulladder_3 (.CI(fulladder_2_co), .A(A5), .B(B5), .S(S5), .CO(fulladder_3_co));
  fullAdder fulladder_4 (.CI(fulladder_3_co), .A(A4), .B(B4), .S(S4), .CO(fulladder_4_co));
  fullAdder fulladder_5 (.CI(fulladder_4_co), .A(A3), .B(B3), .S(S3), .CO(fulladder_5_co));
  fullAdder fulladder_6 (.CI(fulladder_5_co), .A(A2), .B(B2), .S(S2), .CO(fulladder_6_co));
  fullAdder fulladder_7 (.CI(fulladder_6_co), .A(A1), .B(B1), .S(S1), .CO(fulladder_7_co));
  fullAdder fulladder_8 (.CI(fulladder_7_co), .A(A0), .B(B0), .S(S0), .CO(CO));

  // Notes on the sheet:
  //   FullAdder 8bit
endmodule
