// Digital circuit exercise.dig as structural Verilog
module exercise (
  input  B,
  input  A,
  input  A_2,
  input  B_2,
  input  in_5,
  input  in_6,
  input  in_7,
  input  in_8,
  input  in_9,
  input  in_10,
  input  in_11,
  input  [2:0] in_12,
  input  RESET,
  input  SET,
  input  IN,
  input  in_18,
  input  [2:0] in_19,
  input  IN_2,
  input  in_22,
  input  in_23,
  input  IN_3,
  input  QUARTZ,
  output [2:0] out_13,
  output [2:0] out_16,
  output [2:0] out_20,
  output [2:0] out_24,
  output [2:0] out_25,
  output [2:0] out_27
);

  wire and_1_out, and_2_out, and_3_out, and_4_out, and_5_out, counter_1_ovf, counter_2_ovf, nfet_1_s,
       nfet_2_s, nor_1_out, nor_2_out, not_1_out, not_2_out, not_3_out, not_4_out, not_5_out, pfet_1_d;
  wire [2:0] register_1_q;

  PFET pfet_1 (.G(A), .S(B), .D(pfet_1_d));
  NFET nfet_1 (.G(A_2), .D(1'b1), .S(nfet_1_s));
  NFET nfet_2 (.G(nfet_1_s), .D(B_2), .S(nfet_2_s));
  not not_1 (not_1_out, in_8);
  not not_2 (not_2_out, in_9);
  not not_3 (not_3_out, in_10);
  not not_4 (not_4_out, in_11);
  Counter #(.Bits(3)) counter_1 (.en(in_23), .C(in_22), .clr(IN_2), .out(out_24), .ovf(counter_1_ovf));
  Counter #(.Bits(3)) counter_2 (.en(1'b1), .C(QUARTZ), .clr(IN_3), .out(out_27), .ovf(counter_2_ovf));
  LED C (.in(nfet_2_s));
  LED led_1 (.in(in_8));
  LED led_2 (.in(not_1_out));
  LED led_3 (.in(in_9));
  LED led_4 (.in(not_2_out));
  ROM #(.AddrBits(3), .Bits(3)) Cartuccia (.A(in_12), .sel(1'b1), .D(out_13));
  Register #(.Bits(3)) register_1 (.D(in_19), .C(in_18), .en(IN), .Q(register_1_q));
  LED led_5 (.in(counter_2_ovf));
  LED led_6 (.in(pfet_1_d));
  nor nor_1 (nor_1_out, RESET, nor_2_out);
  nor nor_2 (nor_2_out, nor_1_out, SET);
  LED led_7 (.in(counter_1_ovf));
  ROM #(.AddrBits(3), .Bits(3)) Cartuccia_2 (.A(out_24), .sel(1'b1), .D(out_20));
  ROM #(.AddrBits(3), .Bits(3)) Cartuccia_3 (.A(out_27), .sel(1'b1), .D(out_25));
  ROM #(.AddrBits(3), .Bits(3)) Cartuccia_4 (.A(register_1_q), .sel(1'b1), .D(out_16));
  LED led_8 (.in(nor_1_out));
  LED led_9 (.in(nor_2_out));
  not not_5 (not_5_out, in_5);
  and and_1 (and_1_out, in_6, in_7);
  and and_2 (and_2_out, not_3_out, not_4_out);
  and and_3 (and_3_out, in_10, not_4_out);
  and and_4 (and_4_out, in_11, not_4_out);
  and and_5 (and_5_out, in_10, in_11);
  LED led_10 (.in(out_25[0]));
  LED led_11 (.in(not_5_out));
  LED led_12 (.in(and_1_out));
  LED led_13 (.in(and_2_out));
  LED led_14 (.in(and_3_out));
  LED led_15 (.in(and_4_out));
  LED led_16 (.in(and_5_out));

  // Notes on the sheet:
  //   contents of Cartuccia (hex, n*v repeats v):
  //   0,1,1,1,0,1,1
  //   contents of Cartuccia_2 (hex, n*v repeats v):
  //   0,1,1,1,0,1,1
  //   contents of Cartuccia_3 (hex, n*v repeats v):
  //   0,1,1,1,0,1,1
  //   contents of Cartuccia_4 (hex, n*v repeats v):
  //   0,1,1,1,0,1,1
endmodule
